// Logisim project bfProcessor.circ as structural Verilog
module main (
);

  wire clock_1_out, CLR_out, current_noimmediate_1_load_ram, current_noimmediate_1_load_stack,
       current_noimmediate_1_read_kyb, current_noimmediate_1_store_ram, current_noimmediate_1_store_stack,
       current_noimmediate_1_write_enable, keyboard_1_avail;
  wire [3:0] rom_1_data;
  wire [6:0] current_noimmediate_1_ascii_out, keyboard_1_data;
  wire [7:0] current_noimmediate_1_ram_out, current_noimmediate_1_stack_address, ram_2_data;
  wire [15:0] current_noimmediate_1_ram_address, current_noimmediate_1_rom_address, ram_1_data;

  Clock clock_1 (.out(clock_1_out));
  RAM #(.dataWidth(16), .bus("separate")) ram_1 (
    .addr(current_noimmediate_1_stack_address), .din(current_noimmediate_1_rom_address), .data(ram_1_data),
    .str(current_noimmediate_1_store_stack), .clk(clock_1_out), .ld(current_noimmediate_1_load_stack),
    .clr(CLR_out));  // open: sel
  Keyboard keyboard_1 (
    .clk(clock_1_out), .re(current_noimmediate_1_read_kyb), .avail(keyboard_1_avail), .data(keyboard_1_data));  // open: clr
  ROM #(.addrWidth(16), .dataWidth(4)) rom_1 (
    .addr(current_noimmediate_1_rom_address), .data(rom_1_data));  // open: sel
  TTY tty_1 (
    .data(current_noimmediate_1_ascii_out), .clk(clock_1_out), .we(current_noimmediate_1_write_enable),
    .clr(CLR_out));
  CURRENT_NOIMMEDIATE current_noimmediate_1 (
    .LOAD_STACK(current_noimmediate_1_load_stack), .STACK_IN(ram_1_data),
    .STACK_ADDRESS(current_noimmediate_1_stack_address), .STORE_STACK(current_noimmediate_1_store_stack),
    .ROM_ADDRESS(current_noimmediate_1_rom_address), .WRITE_ENABLE(current_noimmediate_1_write_enable),
    .ROM_IN(rom_1_data), .ASCII_OUT(current_noimmediate_1_ascii_out),
    .READ_KYB(current_noimmediate_1_read_kyb), .KYB_BUFFER(keyboard_1_avail), .CLOCK_IN(clock_1_out),
    .ASCII_IN(keyboard_1_data), .RAM_ADDRESS(current_noimmediate_1_ram_address), .RAM_IN(ram_2_data),
    .STORE_RAM(current_noimmediate_1_store_ram), .LOAD_RAM(current_noimmediate_1_load_ram),
    .RAM_OUT(current_noimmediate_1_ram_out));
  RAM #(.addrWidth(16), .bus("separate")) ram_2 (
    .addr(current_noimmediate_1_ram_address), .din(current_noimmediate_1_ram_out), .data(ram_2_data),
    .str(current_noimmediate_1_store_ram), .clk(clock_1_out), .ld(current_noimmediate_1_load_ram),
    .clr(CLR_out));  // open: sel
  Button CLR (.out(CLR_out));

  // Notes on the sheet:
  //   contents of rom_1 (hex, n*v repeats v):
  //   8*3 0 5 1 9 4*3 0 5 1 9 3 3 0 1 9 3 3 3 0 1 9 3 3 3 0 1 9 3 0 4*2 9 4 0 6 a 1 9 3 0 1 9 3 0 1 9 4 0
  //   1 1 9 3 0 5 2 9 6 a 2 9 4 0 6 a 1 1 9 7 1 9 4 4 4 0 7 7*3 0 7 7 3 3 3 0 7 1 1 9 7 2 9 4 0 7 2 9 7 3
  //   3 3 0 7 6*4 0 7 8*4 0 7 1 1 9 3 0 7 1 9 3 3 0 7 b
endmodule

module Decoder (
  input  [3:0] OpCode,
  output Update,
  output _0xA,
  output HALT,
  output _0x09,
  output _0x08,
  output _0x07,
  output _0x06,
  output _0x05,
  output _0x04,
  output _0x03,
  output _0x02,
  output _0x01
);

  wire nor_2_out, nor_3_out, nor_4_out, nor_5_out, nor_6_out, nor_7_out, nor_8_out, not_1_out, not_2_out,
       not_3_out, not_4_out, not_5_out, not_6_out, not_7_out;

  nor nor_1 (Update, OpCode[3], OpCode[2], OpCode[1], OpCode[0]);
  and and_1 (HALT, not_1_out, OpCode[3], OpCode[0], OpCode[1]);
  not not_1 (not_1_out, OpCode[2]);
  not not_2 (not_2_out, OpCode[1]);
  not not_3 (not_3_out, OpCode[2]);
  not not_4 (not_4_out, OpCode[2]);
  and and_2 (_0x08, OpCode[3], not_3_out, not_6_out, not_7_out);
  and and_3 (_0x09, OpCode[3], not_4_out, not_2_out, OpCode[0]);
  not not_5 (not_5_out, OpCode[3]);
  not not_6 (not_6_out, OpCode[1]);
  not not_7 (not_7_out, OpCode[0]);
  and and_4 (_0x07, OpCode[0], OpCode[1], OpCode[2], not_5_out);
  nor nor_2 (nor_2_out, OpCode[3], OpCode[1]);
  nor nor_3 (nor_3_out, OpCode[3], OpCode[0]);
  and and_5 (_0x06, OpCode[2], OpCode[1], nor_3_out);
  and and_6 (_0x05, OpCode[2], nor_2_out, OpCode[0]);
  nor nor_4 (nor_4_out, OpCode[3], OpCode[1], OpCode[0]);
  and and_7 (_0x04, OpCode[2], nor_4_out);
  nor nor_5 (nor_5_out, OpCode[3], OpCode[2]);
  nor nor_6 (nor_6_out, OpCode[3], OpCode[2], OpCode[0]);
  and and_8 (_0x03, OpCode[1], OpCode[0], nor_5_out);
  and and_9 (_0x02, OpCode[1], nor_6_out);
  nor nor_7 (nor_7_out, OpCode[3], OpCode[2], OpCode[1]);
  and and_10 (_0x01, nor_7_out, OpCode[0]);
  and and_11 (_0xA, OpCode[3], OpCode[1], nor_8_out);
  nor nor_8 (nor_8_out, OpCode[2], OpCode[0]);
endmodule

module CPU (
  input  [3:0] ROM_IN,
  input  [15:0] STACK_IN,
  input  [7:0] RAM_IN,
  input  KYB_BUFFER,
  input  CLOCK_IN,
  input  [6:0] ASCII_IN,
  output [15:0] ROM_ADDRESS,
  output WRITE_ENABLE,
  output [6:0] ASCII_OUT,
  output LOAD_STACK,
  output [15:0] RAM_ADDRESS,
  output [7:0] STACK_ADDRESS,
  output STORE_STACK,
  output STORE_RAM,
  output LOAD_RAM,
  output [7:0] RAM_OUT,
  output READ_KYB
);

  wire and_1_out, and_2_out, comparator_1_eq, decoder_1__0x01, decoder_1__0x02, decoder_1__0x03,
       decoder_1__0x04, decoder_1__0x06, decoder_1__0x08, decoder_1__0x09, decoder_1__0xa, decoder_1_halt,
       not_1_out, not_2_out, not_3_out, not_4_out, or_2_out, or_3_out, or_4_out, or_6_out, or_7_out;
  wire [7:0] and_6_out, and_7_out, bit_extender_1_out, bit_extender_2_out, bit_extender_3_out, counter_4_q;
  wire [7:7] or_8_out;
  wire [15:0] adder_1_out;

  or or_1 (READ_KYB, STORE_RAM, decoder_1__0x08);
  Adder #(.width(16)) adder_1 (.a(STACK_IN), .b({16{1'b0}}), .out(adder_1_out), .cin(1'b1));  // open: cout
  and and_1 (and_1_out, not_1_out, not_3_out, 1'b1);
  not not_1 (not_1_out, LOAD_STACK);
  or or_2 (or_2_out, decoder_1__0x06, LOAD_STACK, STORE_STACK);
  not not_2 (not_2_out, KYB_BUFFER);
  and and_2 (and_2_out, decoder_1__0x08, not_2_out);
  Counter #(.width(16), .max('hffff)) counter_1 (
    .load(LOAD_STACK), .D(adder_1_out), .count(and_1_out), .Q(ROM_ADDRESS), .clk(CLOCK_IN));  // open: carry, clr
  Counter counter_2 (
    .load(decoder_1__0x06), .count(or_2_out), .Q(STACK_ADDRESS), .clk(CLOCK_IN));  // open: D, carry, clr
  not not_3 (not_3_out, or_3_out);
  or or_3 (or_3_out, decoder_1_halt, and_2_out);
  and and_3 (LOAD_STACK, not_4_out, decoder_1__0xa);
  // AND_Gate and_4 has open pins: in0=not_3_out, in1=CLOCK_IN, out=open
  Decoder decoder_1 (
    .Update(STORE_RAM), .HALT(decoder_1_halt), .OpCode(ROM_IN), ._0x09(decoder_1__0x09),
    ._0x08(decoder_1__0x08), ._0x07(WRITE_ENABLE), ._0x06(decoder_1__0x06), ._0x05(STORE_STACK),
    ._0x04(decoder_1__0x04), ._0x03(decoder_1__0x03), ._0x02(decoder_1__0x02), ._0x01(decoder_1__0x01),
    ._0xA(decoder_1__0xa));
  or or_4 (or_4_out, decoder_1__0x01, decoder_1__0x02);
  or or_5 (LOAD_RAM, WRITE_ENABLE, decoder_1__0x09);
  assign bit_extender_1_out = {{7{STORE_RAM}}, STORE_RAM};  // Bit_Extender bit_extender_1
  or or_6 (or_6_out, decoder_1__0x03, decoder_1__0x04);
  or or_7 (or_7_out, decoder_1__0x09, decoder_1__0x08, decoder_1__0x04);
  Counter #(.width(16), .max('hffff)) counter_3 (
    .load(decoder_1__0x02), .count(or_4_out), .Q(RAM_ADDRESS), .clk(CLOCK_IN));  // open: D, carry, clr
  assign RAM_OUT = counter_4_q & bit_extender_1_out;  // AND_Gate and_5, 8 bits wide
  assign bit_extender_2_out = {{7{decoder_1__0x08}}, decoder_1__0x08};  // Bit_Extender bit_extender_2
  not not_4 (not_4_out, comparator_1_eq);
  Counter counter_4 (
    .load(or_7_out), .D({or_8_out[7], ASCII_OUT}), .count(or_6_out), .Q(counter_4_q), .clk(CLOCK_IN));  // open: carry, clr
  assign {or_8_out[7], ASCII_OUT} = and_6_out | and_7_out;  // OR_Gate or_8, 8 bits wide
  assign and_6_out = bit_extender_2_out & {1'b0, ASCII_IN};  // AND_Gate and_6, 8 bits wide
  assign bit_extender_3_out = {{7{LOAD_RAM}}, LOAD_RAM};  // Bit_Extender bit_extender_3
  Comparator comparator_1 (.a({8{1'b0}}), .b(counter_4_q), .eq(comparator_1_eq));  // open: gt, lt
  assign and_7_out = bit_extender_3_out & RAM_IN;  // AND_Gate and_7, 8 bits wide
endmodule

module LEGACY_NOINPUT (
  input  [6:0] ASCII_IN,
  output [6:0] ASCII_OUT,
  output WRITE_ENABLE_OUT
);

  wire and_1_out, and_2_out, and_3_out, clock_1_out, comparator_1_eq, decoder_1__0x01, decoder_1__0x02,
       decoder_1__0x03, decoder_1__0x04, decoder_1__0x05, decoder_1__0x06, decoder_1__0x08, decoder_1__0x09,
       decoder_1__0xa, decoder_1_halt, decoder_1_update, not_1_out, not_2_out, not_3_out, or_1_out, or_2_out,
       or_3_out, or_4_out, or_5_out, or_6_out;
  wire [3:0] rom_1_data;
  wire [7:0] adder_1_out, and_4_out, and_5_out, bit_extender_1_out, bit_extender_2_out, counter_1_q,
       counter_2_q, counter_4_q, or_7_out, ram_1_data;
  wire [7:7] ram_2_data;
  wire [15:0] counter_3_q;

  Adder adder_1 (.a(ram_1_data), .b({8{1'b0}}), .out(adder_1_out), .cin(1'b1));  // open: cout
  Counter counter_1 (
    .load(and_2_out), .D(adder_1_out), .count(and_1_out), .Q(counter_1_q), .clk(and_3_out));  // open: carry, clr
  and and_1 (and_1_out, not_1_out, 1'b1);
  not not_1 (not_1_out, and_2_out);
  Counter counter_2 (
    .load(decoder_1__0x06), .count(or_1_out), .Q(counter_2_q), .clk(and_3_out));  // open: D, carry, clr
  or or_1 (or_1_out, decoder_1__0x06, and_2_out, decoder_1__0x05);
  ROM #(.dataWidth(4)) rom_1 (.addr(counter_1_q), .data(rom_1_data));  // open: sel
  RAM #(.bus("separate")) ram_1 (
    .addr(counter_2_q), .din(counter_1_q), .data(ram_1_data), .str(decoder_1__0x05), .clk(and_3_out),
    .ld(and_2_out));  // open: sel, clr
  not not_2 (not_2_out, decoder_1_halt);
  Clock clock_1 (.out(clock_1_out));
  and and_2 (and_2_out, not_3_out, decoder_1__0xa);
  Decoder decoder_1 (
    .Update(decoder_1_update), .HALT(decoder_1_halt), .OpCode(rom_1_data), ._0x09(decoder_1__0x09),
    ._0x08(decoder_1__0x08), ._0x07(WRITE_ENABLE_OUT), ._0x06(decoder_1__0x06), ._0x05(decoder_1__0x05),
    ._0x04(decoder_1__0x04), ._0x03(decoder_1__0x03), ._0x02(decoder_1__0x02), ._0x01(decoder_1__0x01),
    ._0xA(decoder_1__0xa));
  or or_2 (or_2_out, decoder_1_update, decoder_1__0x08);
  and and_3 (and_3_out, not_2_out, clock_1_out);
  assign bit_extender_1_out = {{7{decoder_1__0x08}}, decoder_1__0x08};  // Bit_Extender bit_extender_1
  or or_3 (or_3_out, WRITE_ENABLE_OUT, decoder_1__0x09);
  or or_4 (or_4_out, decoder_1__0x02, decoder_1__0x01);
  or or_5 (or_5_out, decoder_1__0x04, decoder_1__0x09);
  assign and_4_out = bit_extender_1_out & {1'b0, ASCII_IN};  // AND_Gate and_4, 8 bits wide
  not not_3 (not_3_out, comparator_1_eq);
  Counter #(.width(16), .max('hffff)) counter_3 (
    .load(decoder_1__0x02), .count(or_4_out), .Q(counter_3_q), .clk(and_3_out));  // open: D, carry, clr
  or or_6 (or_6_out, decoder_1__0x04, decoder_1__0x03);
  assign bit_extender_2_out = {{7{decoder_1_update}}, decoder_1_update};  // Bit_Extender bit_extender_2
  Counter counter_4 (
    .load(or_5_out), .D({ram_2_data[7], ASCII_OUT}), .count(or_6_out), .Q(counter_4_q), .clk(and_3_out));  // open: carry, clr
  assign and_5_out = bit_extender_2_out & counter_4_q;  // AND_Gate and_5, 8 bits wide
  RAM #(.addrWidth(16), .bus("separate")) ram_2 (
    .addr(counter_3_q), .din(or_7_out), .data({ram_2_data[7], ASCII_OUT}), .str(or_2_out), .clk(and_3_out),
    .ld(or_3_out));  // open: sel, clr
  Comparator comparator_1 (.a({8{1'b0}}), .b(counter_4_q), .eq(comparator_1_eq));  // open: gt, lt
  assign or_7_out = and_4_out | and_5_out;  // OR_Gate or_7, 8 bits wide

  // Notes on the sheet:
  //   contents of rom_1 (hex, n*v repeats v):
  //   8*3 0 5 1 9 4*3 0 5 1 9 3 3 0 1 9 3 3 3 0 1 9 3 3 3 0 1 9 3 0 4*2 9 4 0 6 a 1 9 3 0 1 9 3 0 1 9 4 0
  //   1 1 9 3 0 5 2 9 6 a 2 9 4 0 6 a 1 1 9 7 1 9 4 4 4 0 7 7*3 0 7 7 3 3 3 0 7 1 1 9 7 2 9 4 0 7 2 9 7 3
  //   3 3 0 7 6*4 0 7 8*4 0 7 1 1 9 3 0 7 1 9 3 3 0 7 b
endmodule

module DECODER_V2 (
  input  [3:0] OpCode,
  output STORE_MEM,
  output LOAD_STACK,
  output HALT,
  output LOAD_MEM,
  output INPUT,
  output PRINT,
  output BRKZ,
  output LOOP,
  output VAL_LD,
  output VAL,
  output PRT_LD,
  output PTR
);

  wire nor_2_out, nor_3_out, nor_4_out, nor_5_out, nor_6_out, nor_7_out, nor_8_out, not_1_out, not_2_out,
       not_3_out, not_4_out, not_5_out, not_6_out, not_7_out;

  nor nor_1 (STORE_MEM, OpCode[3], OpCode[2], OpCode[1], OpCode[0]);
  and and_1 (HALT, not_1_out, OpCode[3], OpCode[0], OpCode[1]);
  not not_1 (not_1_out, OpCode[2]);
  not not_2 (not_2_out, OpCode[2]);
  not not_3 (not_3_out, OpCode[1]);
  not not_4 (not_4_out, OpCode[2]);
  and and_2 (INPUT, OpCode[3], not_2_out, not_6_out, not_5_out);
  and and_3 (LOAD_MEM, OpCode[3], not_4_out, not_3_out, OpCode[0]);
  not not_5 (not_5_out, OpCode[0]);
  not not_6 (not_6_out, OpCode[1]);
  not not_7 (not_7_out, OpCode[3]);
  and and_4 (PRINT, OpCode[0], OpCode[1], OpCode[2], not_7_out);
  nor nor_2 (nor_2_out, OpCode[3], OpCode[0]);
  nor nor_3 (nor_3_out, OpCode[3], OpCode[1]);
  and and_5 (BRKZ, OpCode[2], OpCode[1], nor_2_out);
  and and_6 (LOOP, OpCode[2], nor_3_out, OpCode[0]);
  nor nor_4 (nor_4_out, OpCode[3], OpCode[1], OpCode[0]);
  and and_7 (VAL_LD, OpCode[2], nor_4_out);
  nor nor_5 (nor_5_out, OpCode[3], OpCode[2]);
  nor nor_6 (nor_6_out, OpCode[3], OpCode[2], OpCode[0]);
  and and_8 (PRT_LD, OpCode[1], nor_6_out);
  and and_9 (VAL, OpCode[1], OpCode[0], nor_5_out);
  nor nor_7 (nor_7_out, OpCode[3], OpCode[2], OpCode[1]);
  and and_10 (PTR, nor_7_out, OpCode[0]);
  and and_11 (LOAD_STACK, OpCode[3], OpCode[1], nor_8_out);
  nor nor_8 (nor_8_out, OpCode[2], OpCode[0]);
endmodule

module CURRENT_NOIMMEDIATE (
  input  [3:0] ROM_IN,
  input  [15:0] STACK_IN,
  input  [7:0] RAM_IN,
  input  KYB_BUFFER,
  input  CLOCK_IN,
  input  [6:0] ASCII_IN,
  output [15:0] ROM_ADDRESS,
  output WRITE_ENABLE,
  output [6:0] ASCII_OUT,
  output LOAD_STACK,
  output [15:0] RAM_ADDRESS,
  output [7:0] STACK_ADDRESS,
  output STORE_STACK,
  output STORE_RAM,
  output LOAD_RAM,
  output [7:0] RAM_OUT,
  output READ_KYB
);

  wire and_1_out, and_2_out, comparator_1_eq, decoder_1__0x01, decoder_1__0x02, decoder_1__0x03,
       decoder_1__0x04, decoder_1__0x06, decoder_1__0x08, decoder_1__0x09, decoder_1__0xa, decoder_1_halt,
       not_1_out, not_2_out, not_3_out, not_4_out, or_2_out, or_3_out, or_4_out, or_6_out, or_7_out;
  wire [7:0] and_6_out, and_7_out, bit_extender_1_out, bit_extender_2_out, bit_extender_3_out, counter_4_q;
  wire [7:7] or_8_out;
  wire [15:0] adder_1_out;

  or or_1 (READ_KYB, STORE_RAM, decoder_1__0x08);
  Adder #(.width(16)) adder_1 (.a(STACK_IN), .b({16{1'b0}}), .out(adder_1_out), .cin(1'b1));  // open: cout
  and and_1 (and_1_out, not_1_out, not_3_out, 1'b1);
  not not_1 (not_1_out, LOAD_STACK);
  or or_2 (or_2_out, decoder_1__0x06, LOAD_STACK, STORE_STACK);
  and and_2 (and_2_out, decoder_1__0x08, not_2_out);
  not not_2 (not_2_out, KYB_BUFFER);
  Counter #(.width(16), .max('hffff)) counter_1 (
    .load(LOAD_STACK), .D(adder_1_out), .count(and_1_out), .Q(ROM_ADDRESS), .clk(CLOCK_IN));  // open: carry, clr
  Counter counter_2 (
    .load(decoder_1__0x06), .count(or_2_out), .Q(STACK_ADDRESS), .clk(CLOCK_IN));  // open: D, carry, clr
  not not_3 (not_3_out, or_3_out);
  or or_3 (or_3_out, decoder_1_halt, and_2_out);
  and and_3 (LOAD_STACK, not_4_out, decoder_1__0xa);
  // AND_Gate and_4 has open pins: in0=not_3_out, in1=CLOCK_IN, out=open
  Decoder decoder_1 (
    .Update(STORE_RAM), .HALT(decoder_1_halt), .OpCode(ROM_IN), ._0x09(decoder_1__0x09),
    ._0x08(decoder_1__0x08), ._0x07(WRITE_ENABLE), ._0x06(decoder_1__0x06), ._0x05(STORE_STACK),
    ._0x04(decoder_1__0x04), ._0x03(decoder_1__0x03), ._0x02(decoder_1__0x02), ._0x01(decoder_1__0x01),
    ._0xA(decoder_1__0xa));
  or or_4 (or_4_out, decoder_1__0x01, decoder_1__0x02);
  or or_5 (LOAD_RAM, WRITE_ENABLE, decoder_1__0x09);
  assign bit_extender_1_out = {{7{STORE_RAM}}, STORE_RAM};  // Bit_Extender bit_extender_1
  or or_6 (or_6_out, decoder_1__0x03, decoder_1__0x04);
  or or_7 (or_7_out, decoder_1__0x09, decoder_1__0x08, decoder_1__0x04);
  Counter #(.width(16), .max('hffff)) counter_3 (
    .load(decoder_1__0x02), .count(or_4_out), .Q(RAM_ADDRESS), .clk(CLOCK_IN));  // open: D, carry, clr
  assign RAM_OUT = counter_4_q & bit_extender_1_out;  // AND_Gate and_5, 8 bits wide
  assign bit_extender_2_out = {{7{decoder_1__0x08}}, decoder_1__0x08};  // Bit_Extender bit_extender_2
  not not_4 (not_4_out, comparator_1_eq);
  Counter counter_4 (
    .load(or_7_out), .D({or_8_out[7], ASCII_OUT}), .count(or_6_out), .Q(counter_4_q), .clk(CLOCK_IN));  // open: carry, clr
  assign {or_8_out[7], ASCII_OUT} = and_6_out | and_7_out;  // OR_Gate or_8, 8 bits wide
  assign and_6_out = bit_extender_2_out & {1'b0, ASCII_IN};  // AND_Gate and_6, 8 bits wide
  assign bit_extender_3_out = {{7{LOAD_RAM}}, LOAD_RAM};  // Bit_Extender bit_extender_3
  Comparator comparator_1 (.a({8{1'b0}}), .b(counter_4_q), .eq(comparator_1_eq));  // open: gt, lt
  assign and_7_out = bit_extender_3_out & RAM_IN;  // AND_Gate and_7, 8 bits wide
endmodule

module EDGE (
  input  [3:0] ROM_IN,
  input  [15:0] Data,
  input  [15:0] STACK_IN,
  input  [7:0] RAM_IN,
  input  KYB_BUFFER,
  input  CLOCK_IN,
  input  [6:0] ASCII_IN,
  output [15:0] ROM_ADDRESS,
  output WRITE_ENABLE,
  output [6:0] ASCII_OUT,
  output LOAD_STACK,
  output [15:0] RAM_ADDRESS,
  output [7:0] STACK_ADDRESS,
  output STORE_STACK,
  output STORE_RAM,
  output LOAD_RAM,
  output [7:0] RAM_OUT,
  output READ_KYB
);

  wire and_1_out, and_2_out, comparator_1_eq, decoder_v2_1_brkz, decoder_v2_1_halt, decoder_v2_1_input,
       decoder_v2_1_load_mem, decoder_v2_1_load_stack, decoder_v2_1_prt_ld, decoder_v2_1_ptr,
       decoder_v2_1_val, decoder_v2_1_val_ld, not_1_out, not_2_out, not_3_out, not_4_out, or_2_out, or_3_out,
       or_4_out, or_6_out;
  wire [7:0] and_6_out, and_7_out, bit_extender_1_out, bit_extender_2_out, bit_extender_3_out, counter_4_q;
  wire [7:7] or_8_out;
  wire [15:0] adder_1_out;

  or or_1 (READ_KYB, STORE_RAM, decoder_v2_1_input);
  Adder #(.width(16)) adder_1 (.a(STACK_IN), .b({16{1'b0}}), .out(adder_1_out), .cin(1'b1));  // open: cout
  and and_1 (and_1_out, not_1_out, not_3_out, 1'b1);
  not not_1 (not_1_out, LOAD_STACK);
  or or_2 (or_2_out, decoder_v2_1_brkz, LOAD_STACK, STORE_STACK);
  and and_2 (and_2_out, decoder_v2_1_input, not_2_out);
  not not_2 (not_2_out, KYB_BUFFER);
  Counter #(.width(16), .max('hffff)) counter_1 (
    .load(LOAD_STACK), .D(adder_1_out), .count(and_1_out), .Q(ROM_ADDRESS), .clk(CLOCK_IN));  // open: carry, clr
  Counter counter_2 (
    .load(decoder_v2_1_brkz), .count(or_2_out), .Q(STACK_ADDRESS), .clk(CLOCK_IN));  // open: D, carry, clr
  or or_3 (or_3_out, decoder_v2_1_halt, and_2_out);
  not not_3 (not_3_out, or_3_out);
  and and_3 (LOAD_STACK, not_4_out, decoder_v2_1_load_stack);
  // AND_Gate and_4 has open pins: in0=not_3_out, in1=CLOCK_IN, out=open
  DECODER_V2 decoder_v2_1 (
    .STORE_MEM(STORE_RAM), .HALT(decoder_v2_1_halt), .OpCode(ROM_IN), .LOAD_MEM(decoder_v2_1_load_mem),
    .INPUT(decoder_v2_1_input), .PRINT(WRITE_ENABLE), .BRKZ(decoder_v2_1_brkz), .LOOP(STORE_STACK),
    .VAL_LD(decoder_v2_1_val_ld), .VAL(decoder_v2_1_val), .PRT_LD(decoder_v2_1_prt_ld),
    .PTR(decoder_v2_1_ptr), .LOAD_STACK(decoder_v2_1_load_stack));
  or or_4 (or_4_out, Data[0], decoder_v2_1_prt_ld);
  or or_5 (LOAD_RAM, WRITE_ENABLE, decoder_v2_1_load_mem);
  or or_6 (or_6_out, decoder_v2_1_load_mem, decoder_v2_1_input);
  // OR_Gate or_7 is placed but not wired
  Counter #(.width(16), .max('hffff)) counter_3 (
    .load(or_4_out), .D(Data), .count(decoder_v2_1_ptr), .Q(RAM_ADDRESS), .clk(CLOCK_IN));  // open: carry, clr
  assign bit_extender_1_out = {{7{STORE_RAM}}, STORE_RAM};  // Bit_Extender bit_extender_1
  Counter counter_4 (
    .load(or_6_out), .D({or_8_out[7], ASCII_OUT}), .count(decoder_v2_1_val), .Q(counter_4_q), .clk(CLOCK_IN));  // open: carry, clr
  not not_4 (not_4_out, comparator_1_eq);
  assign RAM_OUT = counter_4_q & bit_extender_1_out;  // AND_Gate and_5, 8 bits wide
  assign and_6_out = bit_extender_2_out & {1'b0, ASCII_IN};  // AND_Gate and_6, 8 bits wide
  assign bit_extender_2_out = {{7{decoder_v2_1_input}}, decoder_v2_1_input};  // Bit_Extender bit_extender_2
  Comparator comparator_1 (.a({8{1'b0}}), .b(counter_4_q), .eq(comparator_1_eq));  // open: gt, lt
  assign {or_8_out[7], ASCII_OUT} = and_6_out | and_7_out;  // OR_Gate or_8, 8 bits wide
  assign and_7_out = bit_extender_3_out & RAM_IN;  // AND_Gate and_7, 8 bits wide
  assign bit_extender_3_out = {{7{LOAD_RAM}}, LOAD_RAM};  // Bit_Extender bit_extender_3
endmodule
